// Digital circuit signal generator and character indexer.dig as structural Verilog
module signal_generator_and_character_indexer (
  input  pxl
);

  wire _7402_1_pin1, _7402_1_pin3, _7402_1_pin9, _7402_1_pin10, _7402_1_pin12, _7408_1_pin3, _7408_1_pin6,
       _7408_1_pin8, _7408_1_pin11, _7408_2_pin3, _7408_2_pin5, _7408_2_pin6, _7408_3_pin3, _7420_1_pin5,
       _7420_1_pin6, _74161_1_pin1, _74161_1_pin13, _74161_1_pin14, _74161_1_pin15, _74161_2_pin15,
       _74161_4_pin15, _74161_5_pin15;
  wire [7:0] img_d;
  wire [15:0] _7420_1_pin1;

  _74161 _74161_1 (
    .pin1(_74161_1_pin1), .pin2(pxl), .pin3(1'b0), .pin4(1'b0), .pin5(1'b0), .pin6(1'b0), .pin7(1'b1),
    .pin8(1'b0), .pin9(1'b1), .pin10(1'b1), .pin11(_7420_1_pin1[1]), .pin12(_7420_1_pin1[0]),
    .pin13(_74161_1_pin13), .pin14(_74161_1_pin14), .pin15(_74161_1_pin15), .pin16(1'b1));
  _74161 _74161_2 (
    .pin1(_74161_1_pin1), .pin2(pxl), .pin3(1'b0), .pin4(1'b0), .pin5(1'b0), .pin6(1'b0),
    .pin7(_74161_1_pin15), .pin8(1'b0), .pin9(1'b1), .pin10(1'b1), .pin11(_7420_1_pin1[5]),
    .pin12(_7420_1_pin1[4]), .pin13(_7420_1_pin1[3]), .pin14(_7420_1_pin1[2]), .pin15(_74161_2_pin15),
    .pin16(1'b1));
  _74161 _74161_3 (
    .pin1(_74161_1_pin1), .pin2(pxl), .pin3(1'b0), .pin4(1'b0), .pin5(1'b0), .pin6(1'b0),
    .pin7(_74161_1_pin15), .pin8(1'b0), .pin9(1'b1), .pin10(_74161_2_pin15), .pin13(_7420_1_pin1[7]),
    .pin14(_7420_1_pin1[6]), .pin16(1'b1));  // open: pin11, pin12, pin15
  _7420 _7420_1 (
    .pin1(_7420_1_pin1[15]), .pin2(_7420_1_pin1[9]), .pin4(_7420_1_pin1[8]), .pin5(_7420_1_pin5),
    .pin6(_7420_1_pin6), .pin7(1'b0), .pin8(_74161_1_pin1), .pin9(_7420_1_pin1[3]), .pin10(_7420_1_pin1[6]),
    .pin12(_7420_1_pin1[7]), .pin13(1'b1), .pin14(1'b1));  // open: pin3, pin11
  _74161 _74161_4 (
    .pin1(_7420_1_pin6), .pin2(_74161_1_pin1), .pin3(1'b0), .pin4(1'b0), .pin5(1'b0), .pin6(1'b0),
    .pin7(1'b1), .pin8(1'b0), .pin9(1'b1), .pin10(1'b1), .pin11(_7420_1_pin1[9]), .pin12(_7420_1_pin1[8]),
    .pin14(_7420_1_pin5), .pin15(_74161_4_pin15), .pin16(1'b1));  // open: pin13
  _74161 _74161_5 (
    .pin1(_7420_1_pin6), .pin2(_74161_1_pin1), .pin3(1'b0), .pin4(1'b0), .pin5(1'b0), .pin6(1'b0),
    .pin7(_74161_4_pin15), .pin8(1'b0), .pin9(1'b1), .pin10(1'b1), .pin11(_7420_1_pin1[13]),
    .pin12(_7420_1_pin1[12]), .pin13(_7420_1_pin1[11]), .pin14(_7420_1_pin1[10]), .pin15(_74161_5_pin15),
    .pin16(1'b1));
  _74161 _74161_6 (
    .pin1(_7420_1_pin6), .pin2(_74161_1_pin1), .pin3(1'b0), .pin4(1'b0), .pin5(1'b0), .pin6(1'b0),
    .pin7(_74161_4_pin15), .pin8(1'b0), .pin9(1'b1), .pin10(_74161_5_pin15), .pin13(_7420_1_pin1[15]),
    .pin14(_7420_1_pin1[14]), .pin16(1'b1));  // open: pin11, pin12, pin15
  _7408 _7408_1 (
    .pin1(_74161_1_pin14), .pin2(_74161_1_pin13), .pin3(_7408_1_pin3), .pin4(_7420_1_pin1[0]),
    .pin5(_7420_1_pin1[1]), .pin6(_7408_1_pin6), .pin7(1'b0), .pin8(_7408_1_pin8), .pin9(_7420_1_pin1[2]),
    .pin10(_7420_1_pin1[3]), .pin11(_7408_1_pin11), .pin12(_7420_1_pin1[4]), .pin13(_7420_1_pin1[7]),
    .pin14(1'b1));
  _7408 _7408_2 (
    .pin1(_7408_1_pin6), .pin2(_7408_1_pin3), .pin3(_7408_2_pin3), .pin4(_7408_2_pin3), .pin5(_7408_2_pin5),
    .pin6(_7408_2_pin6), .pin7(1'b0), .pin9(1'b1), .pin10(1'b1), .pin11(_7408_2_pin5), .pin12(_7408_1_pin11),
    .pin13(_7408_1_pin8), .pin14(1'b1));  // open: pin8
  _7402 _7402_1 (
    .pin1(_7402_1_pin1), .pin2(_7408_2_pin6), .pin3(_7402_1_pin3), .pin4(_7402_1_pin3), .pin5(_74161_1_pin1),
    .pin6(_7402_1_pin1), .pin7(1'b0), .pin9(_7402_1_pin9), .pin10(_7402_1_pin10), .pin11(_7402_1_pin10),
    .pin12(_7402_1_pin12), .pin13(_7402_1_pin9), .pin14(1'b1));  // open: pin8
  _7408 _7408_3 (
    .pin1(_7420_1_pin1[7]), .pin2(_7420_1_pin1[5]), .pin3(_7408_3_pin3), .pin4(_7408_3_pin3),
    .pin5(_7420_1_pin1[2]), .pin6(_7402_1_pin12), .pin7(1'b0), .pin9(1'b1), .pin10(1'b1), .pin12(1'b1),
    .pin13(1'b1), .pin14(1'b1));  // open: pin8, pin11
  // _7408 _7408_4: pin names not known
  ROM #(.AddrBits(16), .Bits(8)) img (.A(_7420_1_pin1), .sel(1'b1), .D(img_d));
  Break #(.Cycles(1000000)) hVis (.brk(_7402_1_pin1));
  Break #(.Cycles(1000000)) hSync (.brk(_7402_1_pin9));
  VGA vga_1 (.R(img_d[0]), .G(img_d[3]), .B(img_d[6]), .H(1'b0), .V(1'b0), .C(pxl));

  // Notes on the sheet:
  //   pxl: Hz: 5000
  //   Pulses on frame end
  //   Column counter
  //   Line counter
  //   Pixel coord
  //   bus
  //   R
  //   S
  //   contents of img (hex, n*v repeats v):
  //   256*ff,8*e0,8*1c,8*e0,8*1c,8*e0,8*1c,8*e0,8*1c,8*e0,8*1c,8*e0
  //   ,8*1c,8*e0,8*1c,8*e0,8*1c,8*e0,8*1c,8*e0,8*1c,8*e0,8*1c,8*e0,8*1c
  //   ,8*e0,8*1c,8*e0,8*1c,8*e0,8*1c,8*e0,8*1c,8*ff,8*0,232*ff
endmodule
